# Fritzing sketch Display_todays_temperature (saved by Fritzing 0.9.6b)
breadboards: 1

parts:
  OLED_I2C1 = OLED 128x64 I2C Monochrome Display
  DHT11_1 = DHT11 module
  Part1 = Arduino Uno (Rev3)

nets:
  N1: OLED_I2C1.SDA, Part1.A5/SCL
  N2: OLED_I2C1.SCK, Part1.A4/SDA
  VDD: OLED_I2C1.VDD, DHT11_1.VCC, Part1.5V
  GND: OLED_I2C1.GND, DHT11_1.GND, Part1.GND
  N3: DHT11_1.DATA, Part1.D2

custom parts:
  DHT11 module: https://cdn-learn.adafruit.com/downloads/pdf/dht.pdf DHT11 black pcb module reference by:https://github.com/adafruit/Fritzing-Library/blob/master/parts/DHT11%20Humitidy%20and%20Temperature%20Sensor.fzpz
