# Fritzing sketch LED_and_DHT (saved by Fritzing 0.9.6b)
breadboards: 1

parts:
  Part4 = Arduino Uno (Rev3)
  U4 = WS2812 RGB LED strip
  DHT11_1 = DHT11 module

nets:
  N1: Part4.D12/MISO, U4.DIN
  GND: Part4.GND, U4.GND, DHT11_1.GND
  N2: Part4.D2, DHT11_1.DATA
  VCC: Part4.5V, U4.VCC, DHT11_1.VCC

custom parts:
  WS2812 RGB LED strip: WS2812 strip
  DHT11 module: https://cdn-learn.adafruit.com/downloads/pdf/dht.pdf DHT11 black pcb module reference by:https://github.com/adafruit/Fritzing-Library/blob/master/parts/DHT11%20Humitidy%20and%20Temperature%20Sensor.fzpz
