# Fritzing sketch RFID_Fortune 4 (saved by Fritzing 0.9.6b)
breadboards: 2

parts:
  Part4 = Arduino Uno (Rev3) - ICSP
  Part5 = RFID-RC522-v2
  OLED_I2C3 = OLED 128x64 I2C Monochrome Display  # not connected

nets:
  N1: Part4.ICSP_MOSI, Part4.D11_PWM/MOSI, Part5.MOSI
  N2: Part4.D9_PWM, Part5.RST
  N3: Part4.D10_PWM/SS, Part5.SDA
  N4: Part4.D12/MISO, Part5.MISO
  N5: Part4.D13/SCK, Part5.SCK
  GND: Part4.GND, Part5.GND
  N6: Part4.3V3, Part5.3_3V

custom parts:
  RFID-RC522-v2: A simple China made RFID-RC522 Reader; do check the pin labels, as this is a MFRC522 based clone.
