# Fritzing sketch height calculation (saved by Fritzing 0.9.6b)
breadboards: 1

parts:
  Part2 = Arduino Uno (Rev3)
  OLED_I2C2 = OLED 128x64 I2C Monochrome Display
  HC-SR04_Sensor_1 = HC-SR04 Ultrasonic Distance Sensor

nets:
  5V: Part2.5V, OLED_I2C2.VDD, HC-SR04_Sensor_1.VCC
  GND: Part2.GND, OLED_I2C2.GND
