# Fritzing sketch ledstrip (saved by Fritzing 0.9.6b)
breadboards: 1

parts:
  Part3 = Arduino Uno (Rev3)
  U1 = POT [package=pot_alpha_rv16af-20]
  U2 = WS2812 RGB LED strip

nets:
  N1: Part3.A0, U1.S
  N2: Part3.D12/MISO, U2.DIN
  GND: Part3.GND, U1.A, U2.GND
  5V: Part3.5V, U1.E, U2.VCC

custom parts:
  WS2812 RGB LED strip: WS2812 strip
